# Fritzing sketch Esquematico (saved by Fritzing 0.7.0b)
breadboards: 1

parts:
  U1 = Arduino Mega
  LCD1 = LCD screen
  J1 = Piezo Speaker
  R1 = Rotary Potentiometer (Large) [maximum_resistance=100kΩ package=THT]
  MAX1 = MAX30102
  Sensor_de_Umidade_do_solo1 = Sensor Umidade
  Teclado_Membrana1 = Teclado Membrana

nets:
  N1: U1.AREF, MAX1.SDA
  N2: U1.GND, J1.pin1, MAX1.SCL
  N3: U1.D12, LCD1.RS
  N4: U1.D11, LCD1.E
  N5: U1.D5, LCD1.DB4
  N6: U1.D4, LCD1.DB5
  N7: U1.D3, LCD1.DB6
  N8: U1.D2, LCD1.DB7
  VIN: U1.VIN, LCD1.VDD, LCD1.LED+, R1.leg1, MAX1.VIN, Sensor_de_Umidade_do_solo1.VCC
  N9: U1.A0, Sensor_de_Umidade_do_solo1.A0
  N10: U1.A1, J1.pin2
  N11: U1.D24, Teclado_Membrana1.00
  N12: U1.D25, Teclado_Membrana1.01
  N13: U1.D26, Teclado_Membrana1.02
  N14: U1.D27, Teclado_Membrana1.03
  N15: U1.D32, Teclado_Membrana1.00_C
  N16: U1.D33, Teclado_Membrana1.01_C
  N17: U1.D34, Teclado_Membrana1.02_C
  GND: LCD1.VSS, LCD1.R/W, LCD1.LED-, R1.leg2, MAX1.GND, Sensor_de_Umidade_do_solo1.GND
  N18: LCD1.V0, R1.wiper

custom parts:
  MAX30102: Sensor de Batimentos Cardiacos

// code stored in the sketch: breathing.ino
/* Breathing Sensor
 *  this sketch allows to detect if an infant is breathing or not
 *  this is a ugly hack for the "AngelCare breathing sensor" like this:
 *  http://www.angelcarebaby.com/wp-content/uploads/2013/01/AC401-monitor-sensor-padmoniteur-AC401-detecteur-de-mouvement-600x600.jpg
 *  It has a piezoelectric sensor in the center
 *  in order to make this sketch to work, you will need to connect the positive pole from the sensor to the A0 PIN with a 1mohm 
 *  the other to ground
 *  This is free software, you can modify it and use it the way you like.
 *  Miguel Barajas (@gnuowned) <migbarajas@gmail.com>
 */


// these constants won't change:
const int ledPin = 13;      // led connected to digital pin 13
const int piezoSensor = A0; // the piezo is connected to analog pin 0
const int threshold = 100;  // threshold value to decide when the detected sound is a knock or not
const int incidences = 5;
const int holes = 2;


// these variables will change:
int sensorReading = 0;      // variable to store the value read from the sensor pin
int lastReading = 0;        // varuable to store de last value from the sensor pin
int ledState = LOW;         // variable used to store the last LED status, to toggle the light
int incidencesCount = 0;    // variable to count how many incidences the value from the sensor has been more or less de same (+-10)
int holesCount = 0;         // variable to count false positives and false negatives

void setup() {
  pinMode(ledPin, OUTPUT); // declare the ledPin as as OUTPUT
  Serial.begin(9600);       // use the serial port
}

void loop() {
  // read the sensor and store it in the variable sensorReading:
  sensorReading = analogRead(piezoSensor);
  // print the information in the Serial port (for debug)
  Serial.println(sensorReading);
  Serial.println(lastReading);
  Serial.println(incidencesCount);
  Serial.println(holesCount);
  // if we has been pass the incidences threashold then we have a problem...
  if (incidencesCount >= incidences)
  {
    Serial.println("NO BREATHING DETECTED!!!");
    ledState = !ledState;
    digitalWrite(ledPin, ledState);
  }
  else {
    Serial.println("Breathing detected...");
  }
  //since this is an analog sensor, everytime that we read the sensor the value may be little diferent even if there is no activity
  if (lastReading >= sensorReading - 10  && lastReading <= sensorReading + 10)
  {
    // if the value is more or less the same (+-10, could be more, depending on yours) then we asume we have an incidence
    incidencesCount++;
  }
  else 
  {
    holesCount++;
    if (holesCount >= holes)
    {
      // if there is 3 or more holes (false positive/negatives)
      holesCount=0;
      incidencesCount=0;
    }
  }
  lastReading = sensorReading;
  delay(1000);  // delay to avoid overloading the serial port buffer
}
